# Fritzing sketch leds_buttons (saved by Fritzing 0.9.4)
breadboards: 1

parts:
  S1 = Momentary Switch [package=ksa_sealed_tac_switch]
  S2 = Momentary Switch [package=ksa_sealed_tac_switch]
  Raspberry_Pi_1 = Raspberry Pi B+
  R13 = Resistor [tolerance=±5% resistance=220 package="1206 [SMD]"]
  R15 = Resistor [tolerance=±5% resistance=10 package="1206 [SMD]"]
  R16 = Resistor [tolerance=±5% resistance=220 package="1206 [SMD]"]
  LED1 = LED - 5mm [color="Red (633nm)" package="5 mm [THT]"]
  LED2 = RGB LED (com. cathode, rgb) [package="5 mm [THT]"]

nets:
  N1: S1.1, S2.1, R15.Pin_1
  N2: S1.4, Raspberry_Pi_1.GPIO24
  N3: S2.4, Raspberry_Pi_1.GPIO23
  N4: Raspberry_Pi_1.3v3, R15.Pin_0
  N5: Raspberry_Pi_1.GPIO25, LED2.green_anode
  N6: Raspberry_Pi_1.GPIO18, LED2.blue_anode
  N7: Raspberry_Pi_1.GPIO15, LED2.red_anode
  N8: Raspberry_Pi_1.GPIO14, LED1.anode
  N9: Raspberry_Pi_1.GND, R16.Pin_0
  N10: R13.Pin_0, LED2.common_cathode
  N11: R16.Pin_1, LED1.cathode
