# Fritzing sketch sensors (saved by Fritzing 0.9.4)
breadboards: 1

parts:
  ADC1 = MCP3008 [package=dil16]
  Raspberry_Pi_1 = Raspberry Pi B+
  R1 = Trimmer Potentiometer [maximum_resistance=10kΩ package=THT]
  R2 = Resistor [tolerance=±5% resistance=10 package="1206 [SMD]"]
  R3 = Resistor [tolerance=±5% resistance=10 package="1206 [SMD]"]
  R4 = Resistor [tolerance=±5% resistance=10 package="1206 [SMD]"]
  R5 = Resistor [tolerance=±5% resistance=2.2k package="1206 [SMD]"]
  R6 = Resistor [tolerance=±5% resistance=2.2k package="1206 [SMD]"]
  R7 = Resistor [tolerance=±5% resistance=2.2k package="1206 [SMD]"]
  R8 = Resistor [tolerance=±5% resistance=330 package="1206 [SMD]"]
  R10 = Resistor [tolerance=±5% resistance=330 package="1206 [SMD]"]
  R11 = Resistor [tolerance=±5% resistance=330 package="1206 [SMD]"]
  R12 = Resistor [tolerance=±5% resistance=10 package="1206 [SMD]"]
  R13 = Resistor [tolerance=±5% resistance=220 package="1206 [SMD]"]
  R14 = Temperature Sensor (Thermistor) [thermistor_type=NTC package=THT]
  C1 = Electrolytic Capacitor [capacitance=10μF package="0605 [SMD, electrolytic]"]

nets:
  N1: ADC1.CH0, R2.Pin_0, R5.Pin_1
  N2: ADC1.CH1, R3.Pin_0, R7.Pin_1
  N3: ADC1.CH2, R4.Pin_0, R6.Pin_1
  N4: ADC1.CH3, R1.wiper
  N5: ADC1.CH7, R12.Pin_0, R14.pin_1
  N6: ADC1.DGND, ADC1.AGND, Raspberry_Pi_1.GND, R1.leg1, R13.Pin_1, R14.pin_0, C1.-
  N7: ADC1.CS/SHDN, Raspberry_Pi_1.GPIO8
  N8: ADC1.Din, Raspberry_Pi_1.GPIO10
  N9: ADC1.Dout, Raspberry_Pi_1.GPIO9
  N10: ADC1.CLK, Raspberry_Pi_1.GPIO11
  3V3: ADC1.VREF, ADC1.VDD, Raspberry_Pi_1.3v3, Raspberry_Pi_1.3V3, R1.leg2, R12.Pin_1, C1.+
  N11: R5.Pin_0, R8.Pin_1
  N12: R6.Pin_0, R11.Pin_1
  N13: R7.Pin_0, R10.Pin_1

notes:
  + battery 2 -
  + battery motor -
  + battery 1 -
  Current sensor 1 signal
  Current sensor 2 signal
  + Current sensors supply -
